// Logisim project Digital-Project-1.circ as structural Verilog: 22 circuits, main circuit 16-Bit-Register
module main (
  input  in_1,
  output [17:0] out_2,
  output [17:0] out_3,
  output [17:0] out_4
);

  wire Clock_Memory, Clock_Pc, Clock_Register, controlled_buffer_1_out, controlled_buffer_2_out, EQ, GR,
       IMM_OR_SO2, LESS, MLE, MSE, or_1_out, Writ_Reg_E;
  wire [1:0] ALU_S, PC_DECIDER;
  wire [2:0] B_ADRESS;
  wire [3:0] DES_REG, SO_1, SO_2;
  wire [5:0] IMM;
  wire [9:0] STORE_LOAD_ADRESS;
  wire [13:0] JMP_ADRESS;
  wire [17:0] A, B, b_extend_1_out_2, extend_imm_1_output, Ins_Memory, jmp_extend_1_out_2, multiplexer_1_out,
       multiplexer_2_out, multiplexer_3_out, n18_bit_adder_1_out_3, plus_1_1_out_1;

  Finite_state finite_state_1 (
    .Register(Clock_Register), .Memory(Clock_Memory), .PC(Clock_Pc), .Clock(in_1));  // open: control_unit
  PC pc_1 (
    .coming_instructor(n18_bit_adder_1_out_3), .allow_new_instructor(1'b1), .clock(Clock_Pc),
    .next_instructor(Ins_Memory), .\register_prime_a_input_almasını_sağlar (1'b1));
  _18_Bit_Adder u_18_bit_adder_1 (.in_1(multiplexer_2_out), .out_3(n18_bit_adder_1_out_3), .in_2(Ins_Memory));
  Multiplexer #(.width(18)) multiplexer_1 (.in0(out_2), .in1(out_4), .out(multiplexer_1_out), .sel(MLE));  // open: en
  ROM #(.addrWidth(18), .dataWidth(18)) rom_1 (.addr(Ins_Memory), .data(out_3), .sel(1'b1));
  Plus_1 plus_1_1 (.out_1(plus_1_1_out_1));
  Multiplexer #(.select(2), .width(18)) multiplexer_2 (
    .in0(plus_1_1_out_1), .in1(b_extend_1_out_2), .in2(jmp_extend_1_out_2), .out(multiplexer_2_out),
    .sel(PC_DECIDER));  // open: in3, en
  assign controlled_buffer_1_out = Writ_Reg_E ? Clock_Register : 1'bz;  // Controlled_Buffer controlled_buffer_1
  Control_Unit control_unit_1 (
    .Equal_Com(EQ), .Less_Com(LESS), .JUMP_ADRESS(JMP_ADRESS), .Instruction_Memory_output(out_3),
    .Gr_Com(GR), .ALU_select(ALU_S), .Source2_or_IMM(IMM_OR_SO2), .Memory_Store(MSE), .Memory_Load(MLE),
    .pc_decider(PC_DECIDER), .Write_Register(Writ_Reg_E), .Des_Reg(DES_REG), .Source_R1(SO_1),
    .Source_R2(SO_2), .IMM(IMM), .LOAD_ADRESS(STORE_LOAD_ADRESS), .B_Adress(B_ADRESS));
  _16_Bit_Register u_16_bit_register_1 (
    .Writing_Register(DES_REG), .Output_1(A), .Output_2(B), .writing_enable(Writ_Reg_E),
    .clock(controlled_buffer_1_out), .Write_Data(multiplexer_1_out), .Read_1_Register(SO_1),
    .Read_2_Register(SO_2));
  B_EXTEND b_extend_1 (.in_1(B_ADRESS), .out_2(b_extend_1_out_2));
  Extend_IMM extend_imm_1 (.\input (IMM), .\output (extend_imm_1_output));
  JMP_EXTEND jmp_extend_1 (.in_1(JMP_ADRESS), .out_2(jmp_extend_1_out_2));
  _18_bit_sign_magnitude_comperator u_18_bit_sign_magnitude_comperator_1 (
    .a(A), .b(B), .greater_a_b_p(GR), .equa_a_b_z(EQ), .less_a_b_n(LESS));
  Multiplexer #(.width(18)) multiplexer_3 (
    .in0(B), .in1(extend_imm_1_output), .out(multiplexer_3_out), .sel(IMM_OR_SO2));  // open: en
  ALU ALU (.input_1(A), .input_2(multiplexer_3_out), .\output (out_2), .select_bits(ALU_S));
  RAM #(.addrWidth(10), .dataWidth(18), .bus("separate")) ram_1 (
    .addr(STORE_LOAD_ADRESS), .din(A), .data(out_4), .str(MSE), .sel(1'b1), .clk(controlled_buffer_2_out),
    .ld(MLE));  // open: clr
  assign controlled_buffer_2_out = or_1_out ? Clock_Memory : 1'bz;  // Controlled_Buffer controlled_buffer_2
  or or_1 (or_1_out, MLE, MSE);

  // Other names for the same wires on the sheet: Memory_Load[17:0] = out_4; Memory_Store[17:0] = A

  // Notes on the sheet:
  //   PC
  //   ADDER
  //   Instruction memory
  //   B-extend
  //   JMP-extend
endmodule

module Control_Unit (
  input  Equal_Com,
  input  Less_Com,
  input  [17:0] Instruction_Memory_output,
  input  Gr_Com,
  output [3:0] Des_Reg,
  output [3:0] Source_R1,
  output [3:0] Source_R2,
  output [5:0] IMM,
  output [1:0] ALU_select,
  output Source2_or_IMM,
  output Write_Register,
  output Memory_Load,
  output Memory_Store,
  output [1:0] pc_decider,
  output [13:0] JUMP_ADRESS,
  output [9:0] LOAD_ADRESS,
  output [2:0] B_Adress
);

  wire and_1_out, and_6_out, and_7_out, and_8_out, and_9_out, and_10_out, and_11_out, and_12_out, and_13_out,
       and_14_out, and_15_out, B, not_1_out, not_2_out, not_3_out, not_4_out, not_5_out, not_6_out,
       not_7_out, not_8_out, not_9_out, not_10_out, not_11_out, not_12_out, not_13_out, not_14_out,
       not_15_out, not_16_out, not_17_out, not_18_out, or_2_out, or_3_out;
  wire [0:0] or_4_out;
  wire [1:1] and_5_out;
  wire [2:1] demultiplexer_1_out0_2;
  wire [3:0] demultiplexer_1_out1;
  wire [11:0] demultiplexer_1_out0;

  or or_1 (Write_Register, and_1_out, not_3_out);
  and and_1 (and_1_out, Instruction_Memory_output[0], not_2_out, not_1_out, Instruction_Memory_output[3]);
  not not_1 (not_1_out, Instruction_Memory_output[2]);
  not not_2 (not_2_out, Instruction_Memory_output[1]);
  not not_3 (not_3_out, Instruction_Memory_output[0]);
  Multiplexer #(.select(3), .width(2)) multiplexer_1 (
    .in0(2'b00), .in1(2'b00), .in2(2'b01), .in3(2'b01), .in4(2'b10), .in5(2'b10), .in6(2'b11), .in7(2'b11),
    .out(ALU_select), .sel({demultiplexer_1_out0_2, Source2_or_IMM}));  // open: en
  Multiplexer #(.width(4)) multiplexer_2 (
    .in0(demultiplexer_1_out0[7:4]), .in1(JUMP_ADRESS[3:0]), .out(Des_Reg), .sel(Memory_Load));  // open: en
  Demultiplexer #(.width(18)) demultiplexer_1 (
    .out0({IMM, demultiplexer_1_out0[11:4], Source2_or_IMM, demultiplexer_1_out0_2[1], demultiplexer_1_out0_2[2], demultiplexer_1_out0[0]}),
    .out1({B_Adress, JUMP_ADRESS[10:0], demultiplexer_1_out1}), .in(Instruction_Memory_output),
    .sel(Instruction_Memory_output[0]));  // open: en
  Multiplexer #(.width(4)) multiplexer_3 (
    .in0(demultiplexer_1_out0[11:8]), .in1(JUMP_ADRESS[3:0]), .out(Source_R1),
    .sel(Instruction_Memory_output[0]));  // open: en
  Multiplexer #(.width(4)) multiplexer_4 (
    .in0(IMM[3:0]), .in1(JUMP_ADRESS[7:4]), .out(Source_R2), .sel(Instruction_Memory_output[0]));  // open: en
  not not_4 (not_4_out, demultiplexer_1_out1[2]);
  not not_5 (not_5_out, demultiplexer_1_out1[1]);
  and and_2 (Memory_Store, demultiplexer_1_out1[0], not_5_out, demultiplexer_1_out1[2], not_6_out);
  not not_6 (not_6_out, demultiplexer_1_out1[3]);
  not not_7 (not_7_out, demultiplexer_1_out1[1]);
  and and_3 (Memory_Load, demultiplexer_1_out1[0], not_7_out, not_4_out, demultiplexer_1_out1[3]);
  not not_8 (not_8_out, demultiplexer_1_out1[1]);
  not not_9 (not_9_out, demultiplexer_1_out1[2]);
  not not_10 (not_10_out, demultiplexer_1_out1[3]);
  and and_4 (B, demultiplexer_1_out1[1], demultiplexer_1_out1[2], demultiplexer_1_out1[3]);
  not not_11 (not_11_out, JUMP_ADRESS[8]);
  not not_12 (not_12_out, JUMP_ADRESS[10]);
  not not_13 (not_13_out, JUMP_ADRESS[9]);
  not not_14 (not_14_out, JUMP_ADRESS[10]);
  not not_15 (not_15_out, JUMP_ADRESS[10]);
  not not_16 (not_16_out, JUMP_ADRESS[8]);
  not not_17 (not_17_out, JUMP_ADRESS[9]);
  not not_18 (not_18_out, JUMP_ADRESS[8]);
  and and_5 (and_5_out[1], demultiplexer_1_out1[0], not_8_out, not_9_out, not_10_out);
  and and_6 (and_6_out, not_11_out, JUMP_ADRESS[9], not_12_out);
  and and_7 (and_7_out, JUMP_ADRESS[8], not_13_out, not_14_out);
  and and_8 (and_8_out, JUMP_ADRESS[8], JUMP_ADRESS[9], not_15_out);
  and and_9 (and_9_out, not_16_out, not_17_out, JUMP_ADRESS[10]);
  and and_10 (and_10_out, not_18_out, JUMP_ADRESS[9], JUMP_ADRESS[10]);
  or or_2 (or_2_out, Less_Com, Equal_Com);
  or or_3 (or_3_out, Gr_Com, Equal_Com);
  and and_11 (and_11_out, B, and_6_out, Equal_Com);
  and and_12 (and_12_out, B, and_7_out, Less_Com);
  and and_13 (and_13_out, or_2_out, B, and_8_out);
  and and_14 (and_14_out, B, and_9_out, Gr_Com);
  and and_15 (and_15_out, or_3_out, and_10_out, B);
  Multiplexer #(.width(2)) multiplexer_5 (
    .in0({and_5_out[1], 1'b0}), .in1({1'b0, or_4_out[0]}), .out(pc_decider), .sel(or_4_out[0]));  // open: en
  or or_4 (or_4_out[0], and_11_out, and_12_out, and_13_out, and_14_out, and_15_out);

  assign JUMP_ADRESS[13:11] = B_Adress;
  assign LOAD_ADRESS = {B_Adress, JUMP_ADRESS[10:4]};

  // Other names for the same wires on the sheet: first_bit_control = Instruction_Memory_output[0]; Eq_c = Equal_Com;
  //   LOAD_DEST[3:0] = JUMP_ADRESS[3:0]; OP1[3:0] = JUMP_ADRESS[3:0]; OP2[3:0] = JUMP_ADRESS[7:4]

  // Notes on the sheet:
  //   xor
  //   or
  //   and
  //   LOAD
  //   adder
  //   For alu Part
  //   Destination Register
  //   decide to alu with opcode
  //   Decide ALU operants or others
  //   STORE ADRESS
  //   Decide 
  //   ALU  PART
  //   JUMP,  ST,LD,B
  //   Source Register-1
  //   Source Register-2
  //   IMM
  //   JUMP
  //   Source 1 Registerini ST için Source R için kullanabiliriz.
  //   BEQ
  //   BLT
  //   BLE
  //   BGT
  //   BGE
  //   Burda zaten Memory store 1 olduğu zaman yükleme yapıcaz B ler durumu etkilemez.
  //   DECIDE TO PC 
  //   00 is +1
  //   01 is B
  //   10 is Jump
endmodule

module _16_Bit_Register (
  input  [3:0] Read_1_Register,
  input  [3:0] Writing_Register,
  input  [3:0] Read_2_Register,
  input  writing_enable,
  input  [17:0] Write_Data,
  input  clock,
  output [17:0] Output_1,
  output [17:0] Output_2
);

  wire and_1_out, and_2_out, and_3_out, and_4_out, and_5_out, and_6_out, and_7_out, and_8_out, and_9_out,
       and_10_out, and_11_out, and_12_out, and_13_out, and_14_out, and_15_out, and_16_out, decoder_1_out0,
       decoder_1_out1, decoder_1_out2, decoder_1_out3, decoder_1_out4, decoder_1_out5, decoder_1_out6,
       decoder_1_out7, decoder_1_out8, decoder_1_out9, decoder_1_out10, decoder_1_out11, decoder_1_out12,
       decoder_1_out13, decoder_1_out14, decoder_1_out15;
  wire [17:0] register_1_q, register_2_q, register_3_q, register_4_q, register_5_q, register_6_q,
       register_7_q, register_8_q, register_9_q, register_10_q, register_11_q, register_12_q, register_13_q,
       register_14_q, register_15_q, register_16_q;

  Decoder #(.select(4)) decoder_1 (
    .out0(decoder_1_out0), .out1(decoder_1_out1), .out2(decoder_1_out2), .out3(decoder_1_out3),
    .out4(decoder_1_out4), .out5(decoder_1_out5), .out6(decoder_1_out6), .out7(decoder_1_out7),
    .out8(decoder_1_out8), .out9(decoder_1_out9), .out10(decoder_1_out10), .out11(decoder_1_out11),
    .out12(decoder_1_out12), .out13(decoder_1_out13), .out14(decoder_1_out14), .out15(decoder_1_out15),
    .sel(Writing_Register));  // open: en
  and and_1 (and_1_out, decoder_1_out0, writing_enable);
  and and_2 (and_2_out, decoder_1_out1, writing_enable);
  and and_3 (and_3_out, decoder_1_out2, writing_enable);
  and and_4 (and_4_out, decoder_1_out3, writing_enable);
  and and_5 (and_5_out, decoder_1_out4, writing_enable);
  and and_6 (and_6_out, decoder_1_out5, writing_enable);
  and and_7 (and_7_out, decoder_1_out6, writing_enable);
  and and_8 (and_8_out, decoder_1_out7, writing_enable);
  Register #(.width(18)) register_1 (.D(Write_Data), .en(and_1_out), .Q(register_1_q), .clk(clock));  // open: clr
  Register #(.width(18)) register_2 (.D(Write_Data), .en(and_2_out), .Q(register_2_q), .clk(clock));  // open: clr
  Register #(.width(18)) register_3 (.D(Write_Data), .en(and_3_out), .Q(register_3_q), .clk(clock));  // open: clr
  Register #(.width(18)) register_4 (.D(Write_Data), .en(and_4_out), .Q(register_4_q), .clk(clock));  // open: clr
  Register #(.width(18)) register_5 (.D(Write_Data), .en(and_5_out), .Q(register_5_q), .clk(clock));  // open: clr
  Register #(.width(18)) register_6 (.D(Write_Data), .en(and_6_out), .Q(register_6_q), .clk(clock));  // open: clr
  Register #(.width(18)) register_7 (.D(Write_Data), .en(and_7_out), .Q(register_7_q), .clk(clock));  // open: clr
  Register #(.width(18)) register_8 (.D(Write_Data), .en(and_8_out), .Q(register_8_q), .clk(clock));  // open: clr
  and and_9 (and_9_out, decoder_1_out8, writing_enable);
  and and_10 (and_10_out, decoder_1_out9, writing_enable);
  and and_11 (and_11_out, decoder_1_out10, writing_enable);
  and and_12 (and_12_out, decoder_1_out11, writing_enable);
  and and_13 (and_13_out, decoder_1_out12, writing_enable);
  and and_14 (and_14_out, decoder_1_out13, writing_enable);
  and and_15 (and_15_out, decoder_1_out14, writing_enable);
  and and_16 (and_16_out, decoder_1_out15, writing_enable);
  Register #(.width(18)) register_9 (.D(Write_Data), .en(and_9_out), .Q(register_9_q), .clk(clock));  // open: clr
  Register #(.width(18)) register_10 (.D(Write_Data), .en(and_10_out), .Q(register_10_q), .clk(clock));  // open: clr
  Register #(.width(18)) register_11 (.D(Write_Data), .en(and_11_out), .Q(register_11_q), .clk(clock));  // open: clr
  Register #(.width(18)) register_12 (.D(Write_Data), .en(and_12_out), .Q(register_12_q), .clk(clock));  // open: clr
  Register #(.width(18)) register_13 (.D(Write_Data), .en(and_13_out), .Q(register_13_q), .clk(clock));  // open: clr
  Register #(.width(18)) register_14 (.D(Write_Data), .en(and_14_out), .Q(register_14_q), .clk(clock));  // open: clr
  Register #(.width(18)) register_15 (.D(Write_Data), .en(and_15_out), .Q(register_15_q), .clk(clock));  // open: clr
  Register #(.width(18)) register_16 (.D(Write_Data), .en(and_16_out), .Q(register_16_q), .clk(clock));  // open: clr
  Multiplexer #(.select(4), .width(18)) multiplexer_1 (
    .in0(register_1_q), .in1(register_2_q), .in2(register_3_q), .in3(register_4_q), .in4(register_5_q),
    .in5(register_6_q), .in6(register_7_q), .in7(register_8_q), .in8(register_9_q), .in9(register_10_q),
    .in10(register_11_q), .in11(register_12_q), .in12(register_13_q), .in13(register_14_q),
    .in14(register_15_q), .in15(register_16_q), .out(Output_1), .sel(Read_1_Register));  // open: en
  Multiplexer #(.select(4), .width(18)) multiplexer_2 (
    .in0(register_1_q), .in1(register_2_q), .in2(register_3_q), .in3(register_4_q), .in4(register_5_q),
    .in5(register_6_q), .in6(register_7_q), .in7(register_8_q), .in8(register_9_q), .in9(register_10_q),
    .in10(register_11_q), .in11(register_12_q), .in12(register_13_q), .in13(register_14_q),
    .in14(register_15_q), .in15(register_16_q), .out(Output_2), .sel(Read_2_Register));  // open: en
endmodule

module ALU (
  input  [17:0] input_1,
  input  [17:0] input_2,
  input  [1:0] select_bits,
  output [17:0] \output 
);

  wire [17:0] ADDER_out_3, n18_bit_and_1_out_3, n18_bit_or_1_out_3, XOR_out_3;

  _18_Bit_Adder ADDER (.in_1(input_1), .out_3(ADDER_out_3), .in_2(input_2));
  _18_Bit_AND u_18_bit_and_1 (.in_1(input_1), .in_2(input_2), .out_3(n18_bit_and_1_out_3));
  _18_Bit_OR u_18_bit_or_1 (.in_1(input_1), .in_2(input_2), .out_3(n18_bit_or_1_out_3));
  _18_Bit_XOR XOR (.in_1(input_1), .in_2(input_2), .out_3(XOR_out_3));
  Multiplexer #(.select(2), .width(18)) multiplexer_1 (
    .in0(ADDER_out_3), .in1(n18_bit_and_1_out_3), .in2(n18_bit_or_1_out_3), .in3(XOR_out_3), .out(\output ),
    .sel(select_bits));  // open: en

  // Notes on the sheet:
  //   AND
  //   OR
endmodule

module PC (
  input  [17:0] coming_instructor,
  input  allow_new_instructor,
  input  \register_prime_a_input_almasını_sağlar ,
  input  clock,
  output [17:0] next_instructor
);

  wire [17:0] multiplexer_1_out;

  Multiplexer #(.width(18)) multiplexer_1 (
    .in0(next_instructor), .in1(coming_instructor), .out(multiplexer_1_out), .sel(allow_new_instructor));  // open: en
  Register #(.width(18)) register_1 (
    .D(multiplexer_1_out), .en(\register_prime_a_input_almasını_sağlar ), .Q(next_instructor), .clk(clock),
    .clr(1'b0));
endmodule

module Full_Adder (
  input  a,
  input  b,
  input  C_in,
  output Sum,
  output C_out
);

  wire and_1_out, and_2_out, xor_1_out;

  xor xor_1 (xor_1_out, a, b);
  and and_1 (and_1_out, a, b);
  xor xor_2 (Sum, xor_1_out, C_in);
  and and_2 (and_2_out, xor_1_out, C_in);
  or or_1 (C_out, and_2_out, and_1_out);
endmodule

module Half_Adder (
  input  a,
  input  b,
  output Sum,
  output C_out
);

  xor xor_1 (Sum, a, b);
  and and_1 (C_out, a, b);
endmodule

module _18_Bit_Adder (
  input  [17:0] in_1,
  input  [17:0] in_2,
  output [17:0] out_3
);

  wire FA_2_c_out, FA_3_c_out, FA_4_c_out, FA_5_c_out, FA_6_c_out, FA_7_c_out, FA_8_c_out, FA_9_c_out,
       FA_10_c_out, FA_11_c_out, FA_12_c_out, FA_13_c_out, FA_14_c_out, FA_15_c_out, FA_16_c_out,
       FA_17_c_out, FA_c_out, HA_c_out;

  Half_Adder HA (.a(in_1[0]), .b(in_2[0]), .Sum(out_3[0]), .C_out(HA_c_out));
  Full_Adder FA (.a(in_1[1]), .b(in_2[1]), .C_in(HA_c_out), .Sum(out_3[1]), .C_out(FA_c_out));
  Full_Adder FA_2 (.a(in_1[2]), .b(in_2[2]), .C_in(FA_c_out), .Sum(out_3[2]), .C_out(FA_2_c_out));
  Full_Adder FA_3 (.a(in_1[3]), .b(in_2[3]), .C_in(FA_2_c_out), .Sum(out_3[3]), .C_out(FA_3_c_out));
  Full_Adder FA_4 (.a(in_1[4]), .b(in_2[4]), .C_in(FA_3_c_out), .Sum(out_3[4]), .C_out(FA_4_c_out));
  Full_Adder FA_5 (.a(in_1[5]), .b(in_2[5]), .C_in(FA_4_c_out), .Sum(out_3[5]), .C_out(FA_5_c_out));
  Full_Adder FA_6 (.a(in_1[6]), .b(in_2[6]), .C_in(FA_5_c_out), .Sum(out_3[6]), .C_out(FA_6_c_out));
  Full_Adder FA_7 (.a(in_1[7]), .b(in_2[7]), .C_in(FA_6_c_out), .Sum(out_3[7]), .C_out(FA_7_c_out));
  Full_Adder FA_8 (.a(in_1[8]), .b(in_2[8]), .C_in(FA_7_c_out), .Sum(out_3[8]), .C_out(FA_8_c_out));
  Full_Adder FA_9 (.a(in_1[9]), .b(in_2[9]), .C_in(FA_8_c_out), .Sum(out_3[9]), .C_out(FA_9_c_out));
  Full_Adder FA_10 (.a(in_1[10]), .b(in_2[10]), .C_in(FA_9_c_out), .Sum(out_3[10]), .C_out(FA_10_c_out));
  Full_Adder FA_11 (.a(in_1[11]), .b(in_2[11]), .C_in(FA_10_c_out), .Sum(out_3[11]), .C_out(FA_11_c_out));
  Full_Adder FA_12 (.a(in_1[12]), .b(in_2[12]), .C_in(FA_11_c_out), .Sum(out_3[12]), .C_out(FA_12_c_out));
  Full_Adder FA_13 (.a(in_1[13]), .b(in_2[13]), .C_in(FA_12_c_out), .Sum(out_3[13]), .C_out(FA_13_c_out));
  Full_Adder FA_14 (.a(in_1[14]), .b(in_2[14]), .C_in(FA_13_c_out), .Sum(out_3[14]), .C_out(FA_14_c_out));
  Full_Adder FA_15 (.a(in_1[15]), .b(in_2[15]), .C_in(FA_14_c_out), .Sum(out_3[15]), .C_out(FA_15_c_out));
  Full_Adder FA_16 (.a(in_1[16]), .b(in_2[16]), .C_in(FA_15_c_out), .Sum(out_3[16]), .C_out(FA_16_c_out));
  Full_Adder FA_17 (.a(in_1[17]), .b(in_2[17]), .C_in(FA_16_c_out), .Sum(out_3[17]), .C_out(FA_17_c_out));
endmodule

module _18_Bit_XOR (
  input  [17:0] in_1,
  input  [17:0] in_2,
  output [17:0] out_3
);

  xor xor_1 (out_3[0], in_1[0], in_2[0]);
  xor xor_2 (out_3[1], in_1[1], in_2[1]);
  xor xor_3 (out_3[2], in_1[2], in_2[2]);
  xor xor_4 (out_3[3], in_1[3], in_2[3]);
  xor xor_5 (out_3[4], in_1[4], in_2[4]);
  xor xor_6 (out_3[5], in_1[5], in_2[5]);
  xor xor_7 (out_3[6], in_1[6], in_2[6]);
  xor xor_8 (out_3[7], in_1[7], in_2[7]);
  xor xor_9 (out_3[8], in_1[8], in_2[8]);
  xor xor_10 (out_3[9], in_1[9], in_2[9]);
  xor xor_11 (out_3[10], in_1[10], in_2[10]);
  xor xor_12 (out_3[11], in_1[11], in_2[11]);
  xor xor_13 (out_3[12], in_1[12], in_2[12]);
  xor xor_14 (out_3[13], in_1[13], in_2[13]);
  xor xor_15 (out_3[14], in_1[14], in_2[14]);
  xor xor_16 (out_3[15], in_1[15], in_2[15]);
  xor xor_17 (out_3[16], in_1[16], in_2[16]);
  xor xor_18 (out_3[17], in_1[17], in_2[17]);
endmodule

module _18_Bit_AND (
  input  [17:0] in_1,
  input  [17:0] in_2,
  output [17:0] out_3
);

  and and_1 (out_3[0], in_1[0], in_2[0]);
  and and_2 (out_3[1], in_1[1], in_2[1]);
  and and_3 (out_3[2], in_1[2], in_2[2]);
  and and_4 (out_3[3], in_1[3], in_2[3]);
  and and_5 (out_3[4], in_1[4], in_2[4]);
  and and_6 (out_3[5], in_1[5], in_2[5]);
  and and_7 (out_3[6], in_1[6], in_2[6]);
  and and_8 (out_3[7], in_1[7], in_2[7]);
  and and_9 (out_3[8], in_1[8], in_2[8]);
  and and_10 (out_3[9], in_1[9], in_2[9]);
  and and_11 (out_3[10], in_1[10], in_2[10]);
  and and_12 (out_3[11], in_1[11], in_2[11]);
  and and_13 (out_3[12], in_1[12], in_2[12]);
  and and_14 (out_3[13], in_1[13], in_2[13]);
  and and_15 (out_3[14], in_1[14], in_2[14]);
  and and_16 (out_3[15], in_1[15], in_2[15]);
  and and_17 (out_3[16], in_1[16], in_2[16]);
  and and_18 (out_3[17], in_1[17], in_2[17]);
endmodule

module _18_Bit_OR (
  input  [17:0] in_1,
  input  [17:0] in_2,
  output [17:0] out_3
);

  or or_1 (out_3[0], in_1[0], in_2[0]);
  or or_2 (out_3[1], in_1[1], in_2[1]);
  or or_3 (out_3[2], in_1[2], in_2[2]);
  or or_4 (out_3[3], in_1[3], in_2[3]);
  or or_5 (out_3[4], in_1[4], in_2[4]);
  or or_6 (out_3[5], in_1[5], in_2[5]);
  or or_7 (out_3[6], in_1[6], in_2[6]);
  or or_8 (out_3[7], in_1[7], in_2[7]);
  or or_9 (out_3[8], in_1[8], in_2[8]);
  or or_10 (out_3[9], in_1[9], in_2[9]);
  or or_11 (out_3[10], in_1[10], in_2[10]);
  or or_12 (out_3[11], in_1[11], in_2[11]);
  or or_13 (out_3[12], in_1[12], in_2[12]);
  or or_14 (out_3[13], in_1[13], in_2[13]);
  or or_15 (out_3[14], in_1[14], in_2[14]);
  or or_16 (out_3[15], in_1[15], in_2[15]);
  or or_17 (out_3[16], in_1[16], in_2[16]);
  or or_18 (out_3[17], in_1[17], in_2[17]);
endmodule

module _18_Bit_Magnitude_Comperator (
  input  [17:0] a,
  input  [17:0] b,
  output Greater,
  output Equal,
  output Less
);

  wire a_b_3_out, and_1_out, and_2_out, and_3_out, and_4_out, and_5_out, and_6_out, and_7_out, and_8_out,
       and_9_out, and_10_out, and_11_out, and_12_out, and_13_out, and_14_out, and_15_out, and_16_out,
       and_17_out, and_18_out, and_19_out, and_20_out, and_21_out, and_22_out, and_23_out, and_24_out,
       and_25_out, and_26_out, and_27_out, and_28_out, and_29_out, and_30_out, and_31_out, and_32_out,
       and_33_out, and_34_out, not_1_out, not_2_out, not_3_out, not_4_out, not_5_out, not_6_out, not_7_out,
       not_8_out, not_9_out, not_10_out, not_11_out, not_12_out, not_13_out, not_14_out, not_15_out,
       not_16_out, not_17_out, not_18_out, not_19_out, not_20_out, not_21_out, not_22_out, not_23_out,
       not_24_out, not_25_out, not_26_out, not_27_out, not_28_out, not_29_out, not_30_out, not_31_out,
       not_32_out, not_33_out, not_34_out, xnor_1_out, xnor_2_out, xnor_3_out, xnor_4_out, xnor_5_out,
       xnor_6_out, xnor_7_out, xnor_8_out, xnor_9_out, xnor_10_out, xnor_11_out, xnor_12_out, xnor_13_out,
       xnor_14_out, xnor_15_out, xnor_16_out, xnor_17_out;

  xnor xnor_1 (xnor_1_out, a[16], b[16]);
  xnor xnor_2 (xnor_2_out, a[15], b[15]);
  xnor xnor_3 (xnor_3_out, a[14], b[14]);
  xnor xnor_4 (xnor_4_out, a[13], b[13]);
  xnor xnor_5 (xnor_5_out, a[12], b[12]);
  xnor xnor_6 (xnor_6_out, a[11], b[11]);
  xnor xnor_7 (xnor_7_out, a[10], b[10]);
  xnor xnor_8 (xnor_8_out, a[9], b[9]);
  xnor xnor_9 (xnor_9_out, a[8], b[8]);
  xnor xnor_10 (xnor_10_out, a[7], b[7]);
  xnor xnor_11 (xnor_11_out, a[6], b[6]);
  xnor xnor_12 (xnor_12_out, a[5], b[5]);
  xnor xnor_13 (xnor_13_out, a[4], b[4]);
  xnor xnor_14 (xnor_14_out, a[3], b[3]);
  xnor xnor_15 (xnor_15_out, a[2], b[2]);
  xnor xnor_16 (xnor_16_out, a[1], b[1]);
  xnor xnor_17 (xnor_17_out, a[0], b[0]);
  not not_1 (not_1_out, a[2]);
  not not_2 (not_2_out, a[1]);
  not not_3 (not_3_out, a[0]);
  not not_4 (not_4_out, a[16]);
  not not_5 (not_5_out, a[15]);
  not not_6 (not_6_out, a[14]);
  not not_7 (not_7_out, a[13]);
  not not_8 (not_8_out, a[12]);
  not not_9 (not_9_out, a[11]);
  not not_10 (not_10_out, a[10]);
  not not_11 (not_11_out, a[9]);
  not not_12 (not_12_out, a[8]);
  not not_13 (not_13_out, a[7]);
  not not_14 (not_14_out, a[6]);
  not not_15 (not_15_out, a[5]);
  not not_16 (not_16_out, a[4]);
  not not_17 (not_17_out, a[3]);
  not not_18 (not_18_out, b[2]);
  not not_19 (not_19_out, b[1]);
  not not_20 (not_20_out, b[0]);
  and and_1 (and_1_out, b[16], not_4_out);
  and and_2 (and_2_out, b[15], not_5_out, xnor_2_out);
  and and_3 (and_3_out, b[14], not_6_out, xnor_1_out, xnor_2_out);
  and and_4 (and_4_out, b[13], not_7_out, xnor_1_out, xnor_2_out, xnor_3_out);
  and and_5 (and_5_out, b[12], not_8_out, xnor_1_out, xnor_2_out, xnor_3_out, xnor_4_out);
  and and_6 (and_6_out, b[11], not_9_out, xnor_1_out, xnor_2_out, xnor_3_out, xnor_4_out, xnor_5_out);
  and and_7 (and_7_out, b[10], not_10_out, xnor_1_out, xnor_2_out, xnor_3_out, xnor_4_out, xnor_5_out, xnor_6_out);
  and and_8 (and_8_out, b[9], not_11_out, xnor_1_out, xnor_2_out, xnor_3_out, xnor_4_out, xnor_5_out, xnor_6_out, xnor_7_out);
  and and_9 (and_9_out, b[8], not_12_out, xnor_1_out, xnor_2_out, xnor_3_out, xnor_4_out, xnor_5_out, xnor_6_out, xnor_7_out, xnor_8_out);
  and and_10 (and_10_out, b[7], not_13_out, xnor_1_out, xnor_2_out, xnor_3_out, xnor_4_out, xnor_5_out, xnor_6_out, xnor_7_out, xnor_8_out, xnor_9_out);
  and and_11 (and_11_out, b[6], not_14_out, xnor_1_out, xnor_2_out, xnor_3_out, xnor_4_out, xnor_5_out, xnor_6_out, xnor_7_out, xnor_8_out, xnor_9_out, xnor_10_out);
  and and_12 (and_12_out, b[5], not_15_out, xnor_1_out, xnor_2_out, xnor_3_out, xnor_4_out, xnor_5_out, xnor_6_out, xnor_7_out, xnor_8_out, xnor_9_out, xnor_10_out, xnor_11_out);
  and and_13 (and_13_out, b[4], not_16_out, xnor_1_out, xnor_2_out, xnor_3_out, xnor_4_out, xnor_5_out, xnor_6_out, xnor_7_out, xnor_8_out, xnor_9_out, xnor_10_out, xnor_11_out, xnor_12_out);
  and and_14 (and_14_out, b[3], not_17_out, xnor_1_out, xnor_2_out, xnor_3_out, xnor_4_out, xnor_5_out, xnor_6_out, xnor_7_out, xnor_8_out, xnor_9_out, xnor_10_out, xnor_11_out, xnor_12_out, xnor_13_out);
  and and_15 (and_15_out, b[2], not_1_out, xnor_1_out, xnor_2_out, xnor_3_out, xnor_4_out, xnor_5_out, xnor_6_out, xnor_7_out, xnor_8_out, xnor_9_out, xnor_10_out, xnor_11_out, xnor_12_out, xnor_13_out, xnor_14_out);
  and and_16 (and_16_out, b[1], not_2_out, xnor_1_out, xnor_2_out, xnor_3_out, xnor_4_out, xnor_5_out, xnor_6_out, xnor_7_out, xnor_8_out, xnor_9_out, xnor_10_out, xnor_11_out, xnor_12_out, xnor_13_out, xnor_14_out, xnor_15_out);
  and and_17 (and_17_out, b[0], not_3_out, xnor_1_out, xnor_2_out, xnor_3_out, xnor_4_out, xnor_5_out, xnor_6_out, xnor_7_out, xnor_8_out, xnor_9_out, xnor_10_out, xnor_11_out, xnor_12_out, xnor_13_out, xnor_14_out, xnor_15_out, xnor_16_out);
  not not_21 (not_21_out, b[3]);
  not not_22 (not_22_out, b[6]);
  not not_23 (not_23_out, b[5]);
  not not_24 (not_24_out, b[4]);
  not not_25 (not_25_out, b[13]);
  not not_26 (not_26_out, b[12]);
  not not_27 (not_27_out, b[11]);
  not not_28 (not_28_out, b[10]);
  not not_29 (not_29_out, b[9]);
  not not_30 (not_30_out, b[8]);
  not not_31 (not_31_out, b[7]);
  not not_32 (not_32_out, b[16]);
  not not_33 (not_33_out, b[15]);
  not not_34 (not_34_out, b[14]);
  or a_b (Less, and_1_out, and_2_out, and_3_out, and_4_out, and_5_out, and_6_out, and_7_out, and_8_out, and_17_out, and_9_out, and_10_out, and_11_out, and_12_out, and_13_out, and_14_out, and_15_out, and_16_out);
  and and_18 (and_18_out, not_32_out, a[16]);
  and and_19 (and_19_out, not_33_out, xnor_1_out, a[15]);
  and and_20 (and_20_out, not_34_out, xnor_1_out, xnor_2_out, a[14]);
  and and_21 (and_21_out, not_25_out, xnor_1_out, xnor_2_out, xnor_3_out, a[13]);
  and and_22 (and_22_out, not_26_out, xnor_1_out, xnor_2_out, xnor_3_out, xnor_4_out, a[12]);
  and and_23 (and_23_out, not_27_out, xnor_1_out, xnor_2_out, xnor_3_out, xnor_4_out, xnor_5_out, a[11]);
  and and_24 (and_24_out, not_28_out, xnor_1_out, xnor_2_out, xnor_3_out, xnor_4_out, xnor_6_out, a[10]);
  and and_25 (and_25_out, not_29_out, xnor_1_out, xnor_2_out, xnor_3_out, xnor_4_out, xnor_5_out, xnor_6_out, xnor_7_out, a[9]);
  and and_26 (and_26_out, not_30_out, xnor_1_out, xnor_2_out, xnor_3_out, xnor_4_out, xnor_5_out, xnor_6_out, xnor_8_out, xnor_7_out, a[8]);
  and and_27 (and_27_out, not_31_out, xnor_1_out, xnor_2_out, xnor_3_out, xnor_4_out, xnor_5_out, xnor_6_out, xnor_7_out, xnor_8_out, xnor_9_out, a[7]);
  and and_28 (and_28_out, not_22_out, xnor_1_out, xnor_2_out, xnor_3_out, xnor_4_out, xnor_5_out, xnor_6_out, xnor_7_out, xnor_8_out, xnor_9_out, xnor_10_out, a[6]);
  and and_29 (and_29_out, not_23_out, xnor_1_out, xnor_2_out, xnor_3_out, xnor_4_out, xnor_5_out, xnor_6_out, xnor_7_out, xnor_8_out, xnor_9_out, xnor_10_out, xnor_11_out, a[5]);
  and and_30 (and_30_out, not_24_out, xnor_1_out, xnor_2_out, xnor_3_out, xnor_4_out, xnor_5_out, xnor_6_out, xnor_7_out, xnor_8_out, xnor_9_out, xnor_10_out, xnor_11_out, xnor_12_out, a[4]);
  and and_31 (and_31_out, not_21_out, xnor_1_out, xnor_2_out, xnor_3_out, xnor_4_out, xnor_5_out, xnor_6_out, xnor_7_out, xnor_8_out, xnor_9_out, xnor_10_out, xnor_11_out, xnor_12_out, xnor_13_out, a[3]);
  and and_32 (and_32_out, not_18_out, xnor_1_out, xnor_2_out, xnor_3_out, xnor_4_out, xnor_5_out, xnor_6_out, xnor_7_out, xnor_8_out, xnor_9_out, xnor_10_out, xnor_11_out, xnor_12_out, xnor_13_out, xnor_14_out, a[2]);
  and and_33 (and_33_out, not_19_out, xnor_1_out, xnor_2_out, xnor_3_out, xnor_4_out, xnor_5_out, xnor_6_out, xnor_7_out, xnor_8_out, xnor_9_out, xnor_10_out, xnor_11_out, xnor_12_out, xnor_13_out, xnor_14_out, xnor_15_out, a[1]);
  and and_34 (and_34_out, not_20_out, xnor_1_out, xnor_2_out, xnor_3_out, xnor_4_out, xnor_5_out, xnor_6_out, xnor_7_out, xnor_8_out, xnor_9_out, xnor_10_out, xnor_11_out, xnor_12_out, xnor_13_out, xnor_14_out, xnor_15_out, xnor_16_out, a[0]);
  and a_b_2 (Equal, xnor_1_out, xnor_2_out, xnor_3_out, xnor_4_out, xnor_5_out, xnor_6_out, xnor_7_out, xnor_8_out, xnor_9_out, xnor_10_out, xnor_11_out, xnor_12_out, xnor_13_out, xnor_14_out, xnor_15_out, xnor_16_out, xnor_17_out);
  not not_35 (Greater, a_b_3_out);
  nor a_b_3 (a_b_3_out, and_18_out, and_19_out, and_20_out, and_21_out, and_22_out, and_23_out, and_24_out, and_25_out, and_34_out, and_26_out, and_27_out, and_28_out, and_29_out, and_30_out, and_31_out, and_32_out, and_33_out);
  // NOT_Gate not_36 is placed but not wired
endmodule

module Extend_IMM (
  input  [5:0] \input ,
  output [17:0] \output 
);

  Multiplexer #(.width(12)) multiplexer_1 (
    .in0({12{1'b0}}), .in1({12{1'b1}}), .out(\output [17:6]), .sel(\input [5]));  // open: en

  assign \output [5:0] = \input ;
endmodule

module B_EXTEND (
  input  [2:0] in_1,
  output [17:0] out_2
);

  Multiplexer #(.width(15)) multiplexer_1 (
    .in0({15{1'b0}}), .in1({15{1'b1}}), .out(out_2[17:3]), .sel(in_1[2]));  // open: en

  assign out_2[2:0] = in_1;
endmodule

module JMP_EXTEND (
  input  [13:0] in_1,
  output [17:0] out_2
);

  Multiplexer #(.width(4)) multiplexer_1 (
    .in0(4'b0000), .in1(4'b1111), .out(out_2[17:14]), .sel(in_1[13]));  // open: en

  assign out_2[13:0] = in_1;
endmodule

module Plus_1 (
  output [17:0] out_1
);


  assign out_1 = 18'h1;
endmodule

module Finite_Register (
  input  clock,
  output [1:0] next_instructor
);

  wire [1:0] adder_1_out, multiplexer_1_out;

  Multiplexer #(.width(2)) multiplexer_1 (
    .in0(next_instructor), .in1(adder_1_out), .out(multiplexer_1_out), .sel(1'b1));  // open: en
  Adder #(.width(2)) adder_1 (.a(next_instructor), .b(2'b01), .out(adder_1_out));  // open: cin, cout
  Register #(.width(2)) register_1 (.D(multiplexer_1_out), .en(1'b1), .Q(next_instructor), .clk(clock), .clr(1'b0));
endmodule

module Finite_state (
  input  Clock,
  output control_unit,
  output Register,
  output Memory,
  output PC
);

  wire [1:0] finite_register_1_next_instructor;

  Finite_Register finite_register_1 (.clock(Clock), .next_instructor(finite_register_1_next_instructor));
  Demultiplexer #(.select(2)) demultiplexer_1 (
    .out0(control_unit), .out1(Register), .out2(Memory), .out3(PC), .in(1'b1),
    .sel(finite_register_1_next_instructor));  // open: en
endmodule

module Control_Unit_Clock (
  input  [17:0] coming_instructor,
  input  clock,
  output [17:0] next_instructor
);

  wire [17:0] multiplexer_1_out;

  Multiplexer #(.width(18)) multiplexer_1 (
    .in0(next_instructor), .in1(coming_instructor), .out(multiplexer_1_out), .sel(1'b1));  // open: en
  Register #(.width(18)) register_1 (.D(multiplexer_1_out), .en(1'b1), .Q(next_instructor), .clk(clock), .clr(1'b0));
endmodule

module deneme1 (
  input  [17:0] coming_instructor,
  input  clock,
  output [17:0] next_instructor
);

  wire [17:0] multiplexer_1_out;

  Multiplexer #(.width(18)) multiplexer_1 (
    .in0(next_instructor), .in1(coming_instructor), .out(multiplexer_1_out), .sel(1'b1));  // open: en
  Register #(.width(18)) register_1 (.D(multiplexer_1_out), .en(1'b1), .Q(next_instructor), .clk(clock), .clr(1'b0));
endmodule

module _18_bit_unsigned_magnitude_comperator (
  input  [17:0] a,
  input  [17:0] b,
  output greater,
  output equal,
  output less
);

  wire a_b_3_out, and_1_out, and_2_out, and_3_out, and_4_out, and_5_out, and_6_out, and_7_out, and_8_out,
       and_9_out, and_10_out, and_11_out, and_12_out, and_13_out, and_14_out, and_15_out, and_16_out,
       and_17_out, and_18_out, and_19_out, and_20_out, and_21_out, and_22_out, and_23_out, and_24_out,
       and_25_out, and_26_out, and_27_out, and_28_out, and_29_out, and_30_out, and_31_out, and_32_out,
       and_33_out, and_34_out, and_35_out, and_36_out, not_1_out, not_2_out, not_3_out, not_4_out, not_5_out,
       not_6_out, not_7_out, not_8_out, not_9_out, not_10_out, not_11_out, not_12_out, not_13_out,
       not_14_out, not_15_out, not_16_out, not_17_out, not_18_out, not_19_out, not_20_out, not_21_out,
       not_22_out, not_23_out, not_24_out, not_25_out, not_26_out, not_27_out, not_28_out, not_29_out,
       not_30_out, not_31_out, not_32_out, not_33_out, not_34_out, not_35_out, not_36_out, xnor_1_out,
       xnor_2_out, xnor_3_out, xnor_4_out, xnor_5_out, xnor_6_out, xnor_7_out, xnor_8_out, xnor_9_out,
       xnor_10_out, xnor_11_out, xnor_12_out, xnor_13_out, xnor_14_out, xnor_15_out, xnor_16_out,
       xnor_17_out, xnor_18_out;

  xnor xnor_1 (xnor_1_out, a[17], b[17]);
  xnor xnor_2 (xnor_2_out, a[16], b[16]);
  xnor xnor_3 (xnor_3_out, a[15], b[15]);
  xnor xnor_4 (xnor_4_out, a[14], b[14]);
  xnor xnor_5 (xnor_5_out, a[13], b[13]);
  xnor xnor_6 (xnor_6_out, a[12], b[12]);
  xnor xnor_7 (xnor_7_out, a[11], b[11]);
  xnor xnor_8 (xnor_8_out, a[10], b[10]);
  xnor xnor_9 (xnor_9_out, a[9], b[9]);
  xnor xnor_10 (xnor_10_out, a[8], b[8]);
  xnor xnor_11 (xnor_11_out, a[7], b[7]);
  xnor xnor_12 (xnor_12_out, a[6], b[6]);
  xnor xnor_13 (xnor_13_out, a[5], b[5]);
  xnor xnor_14 (xnor_14_out, a[4], b[4]);
  xnor xnor_15 (xnor_15_out, a[3], b[3]);
  xnor xnor_16 (xnor_16_out, a[2], b[2]);
  xnor xnor_17 (xnor_17_out, a[1], b[1]);
  xnor xnor_18 (xnor_18_out, a[0], b[0]);
  not not_1 (not_1_out, a[4]);
  not not_2 (not_2_out, a[3]);
  not not_3 (not_3_out, a[2]);
  not not_4 (not_4_out, a[1]);
  not not_5 (not_5_out, a[0]);
  not not_6 (not_6_out, a[17]);
  not not_7 (not_7_out, a[16]);
  not not_8 (not_8_out, a[15]);
  not not_9 (not_9_out, a[14]);
  not not_10 (not_10_out, a[13]);
  not not_11 (not_11_out, a[12]);
  not not_12 (not_12_out, a[11]);
  not not_13 (not_13_out, a[10]);
  not not_14 (not_14_out, a[9]);
  not not_15 (not_15_out, a[8]);
  not not_16 (not_16_out, a[7]);
  not not_17 (not_17_out, a[6]);
  not not_18 (not_18_out, a[5]);
  not not_19 (not_19_out, b[0]);
  not not_20 (not_20_out, b[2]);
  not not_21 (not_21_out, b[1]);
  and and_1 (and_1_out, b[17], not_6_out);
  and and_2 (and_2_out, b[16], not_7_out, xnor_1_out);
  and and_3 (and_3_out, b[15], not_8_out, xnor_1_out, xnor_3_out);
  and and_4 (and_4_out, b[14], not_9_out, xnor_1_out, xnor_2_out, xnor_3_out);
  and and_5 (and_5_out, b[13], not_10_out, xnor_1_out, xnor_2_out, xnor_3_out, xnor_4_out);
  and and_6 (and_6_out, b[12], not_11_out, xnor_1_out, xnor_2_out, xnor_3_out, xnor_4_out, xnor_5_out);
  and and_7 (and_7_out, b[11], not_12_out, xnor_1_out, xnor_2_out, xnor_3_out, xnor_4_out, xnor_5_out, xnor_6_out);
  and and_8 (and_8_out, b[10], not_13_out, xnor_1_out, xnor_2_out, xnor_3_out, xnor_4_out, xnor_5_out, xnor_6_out, xnor_7_out);
  and and_9 (and_9_out, b[9], not_14_out, xnor_1_out, xnor_2_out, xnor_3_out, xnor_4_out, xnor_5_out, xnor_6_out, xnor_7_out, xnor_8_out);
  and and_10 (and_10_out, b[8], not_15_out, xnor_1_out, xnor_2_out, xnor_3_out, xnor_4_out, xnor_5_out, xnor_6_out, xnor_7_out, xnor_8_out, xnor_9_out);
  and and_11 (and_11_out, b[7], not_16_out, xnor_1_out, xnor_2_out, xnor_3_out, xnor_4_out, xnor_5_out, xnor_6_out, xnor_7_out, xnor_8_out, xnor_9_out, xnor_10_out);
  and and_12 (and_12_out, b[6], not_17_out, xnor_1_out, xnor_2_out, xnor_3_out, xnor_4_out, xnor_5_out, xnor_6_out, xnor_7_out, xnor_8_out, xnor_9_out, xnor_10_out, xnor_11_out);
  and and_13 (and_13_out, b[5], not_18_out, xnor_1_out, xnor_2_out, xnor_3_out, xnor_4_out, xnor_5_out, xnor_6_out, xnor_7_out, xnor_8_out, xnor_9_out, xnor_10_out, xnor_11_out, xnor_12_out);
  and and_14 (and_14_out, b[4], not_1_out, xnor_1_out, xnor_2_out, xnor_3_out, xnor_4_out, xnor_5_out, xnor_6_out, xnor_7_out, xnor_8_out, xnor_9_out, xnor_10_out, xnor_11_out, xnor_12_out, xnor_13_out);
  and and_15 (and_15_out, b[3], not_2_out, xnor_1_out, xnor_2_out, xnor_3_out, xnor_4_out, xnor_5_out, xnor_6_out, xnor_7_out, xnor_8_out, xnor_9_out, xnor_10_out, xnor_11_out, xnor_12_out, xnor_13_out, xnor_14_out);
  and and_16 (and_16_out, b[2], not_3_out, xnor_1_out, xnor_2_out, xnor_3_out, xnor_4_out, xnor_5_out, xnor_6_out, xnor_7_out, xnor_8_out, xnor_9_out, xnor_10_out, xnor_11_out, xnor_12_out, xnor_13_out, xnor_14_out, xnor_15_out);
  and and_17 (and_17_out, b[1], not_4_out, xnor_1_out, xnor_2_out, xnor_3_out, xnor_4_out, xnor_5_out, xnor_6_out, xnor_7_out, xnor_8_out, xnor_9_out, xnor_10_out, xnor_11_out, xnor_12_out, xnor_13_out, xnor_14_out, xnor_15_out, xnor_16_out);
  and and_18 (and_18_out, b[0], not_5_out, xnor_1_out, xnor_2_out, xnor_3_out, xnor_4_out, xnor_5_out, xnor_6_out, xnor_7_out, xnor_8_out, xnor_9_out, xnor_10_out, xnor_11_out, xnor_12_out, xnor_13_out, xnor_14_out, xnor_15_out, xnor_16_out, xnor_17_out);
  not not_22 (not_22_out, b[4]);
  not not_23 (not_23_out, b[3]);
  not not_24 (not_24_out, b[6]);
  not not_25 (not_25_out, b[5]);
  not not_26 (not_26_out, b[16]);
  not not_27 (not_27_out, b[15]);
  not not_28 (not_28_out, b[14]);
  not not_29 (not_29_out, b[13]);
  not not_30 (not_30_out, b[12]);
  not not_31 (not_31_out, b[11]);
  not not_32 (not_32_out, b[10]);
  not not_33 (not_33_out, b[9]);
  not not_34 (not_34_out, b[8]);
  not not_35 (not_35_out, b[7]);
  not not_36 (not_36_out, b[17]);
  or a_b (less, and_1_out, and_2_out, and_3_out, and_4_out, and_5_out, and_6_out, and_7_out, and_8_out, and_9_out, and_10_out, and_11_out, and_12_out, and_13_out, and_14_out, and_15_out, and_16_out, and_17_out, and_18_out);
  and and_19 (and_19_out, not_36_out, a[17]);
  and and_20 (and_20_out, not_26_out, xnor_1_out, a[16]);
  and and_21 (and_21_out, not_27_out, xnor_1_out, xnor_2_out, a[15]);
  and and_22 (and_22_out, not_28_out, xnor_1_out, xnor_2_out, xnor_3_out, a[14]);
  and and_23 (and_23_out, not_29_out, xnor_1_out, xnor_2_out, xnor_3_out, xnor_4_out, a[13]);
  and and_24 (and_24_out, not_30_out, xnor_1_out, xnor_2_out, xnor_3_out, xnor_4_out, xnor_5_out, a[12]);
  and and_25 (and_25_out, not_31_out, xnor_1_out, xnor_2_out, xnor_3_out, xnor_4_out, xnor_5_out, xnor_6_out, a[11]);
  and and_26 (and_26_out, not_32_out, xnor_1_out, xnor_2_out, xnor_3_out, xnor_4_out, xnor_5_out, xnor_7_out, a[10]);
  and and_27 (and_27_out, not_33_out, xnor_1_out, xnor_2_out, xnor_3_out, xnor_4_out, xnor_5_out, xnor_6_out, xnor_7_out, xnor_8_out, a[9]);
  and and_28 (and_28_out, not_34_out, xnor_1_out, xnor_2_out, xnor_3_out, xnor_4_out, xnor_5_out, xnor_6_out, xnor_7_out, xnor_9_out, xnor_8_out, a[8]);
  and and_29 (and_29_out, not_35_out, xnor_1_out, xnor_2_out, xnor_3_out, xnor_4_out, xnor_5_out, xnor_6_out, xnor_7_out, xnor_8_out, xnor_9_out, xnor_10_out, a[7]);
  and and_30 (and_30_out, not_24_out, xnor_1_out, xnor_2_out, xnor_3_out, xnor_4_out, xnor_5_out, xnor_6_out, xnor_7_out, xnor_8_out, xnor_9_out, xnor_10_out, xnor_11_out, a[6]);
  and and_31 (and_31_out, not_25_out, xnor_1_out, xnor_2_out, xnor_3_out, xnor_4_out, xnor_5_out, xnor_6_out, xnor_7_out, xnor_8_out, xnor_9_out, xnor_10_out, xnor_11_out, xnor_12_out, a[5]);
  and and_32 (and_32_out, not_22_out, xnor_1_out, xnor_2_out, xnor_3_out, xnor_4_out, xnor_5_out, xnor_6_out, xnor_7_out, xnor_8_out, xnor_9_out, xnor_10_out, xnor_11_out, xnor_12_out, xnor_13_out, a[4]);
  and and_33 (and_33_out, not_23_out, xnor_1_out, xnor_2_out, xnor_3_out, xnor_4_out, xnor_5_out, xnor_6_out, xnor_7_out, xnor_8_out, xnor_9_out, xnor_10_out, xnor_11_out, xnor_12_out, xnor_13_out, xnor_14_out, a[3]);
  and and_34 (and_34_out, not_20_out, xnor_1_out, xnor_2_out, xnor_3_out, xnor_4_out, xnor_5_out, xnor_6_out, xnor_7_out, xnor_8_out, xnor_9_out, xnor_10_out, xnor_11_out, xnor_12_out, xnor_13_out, xnor_14_out, xnor_15_out, a[2]);
  and and_35 (and_35_out, not_21_out, xnor_1_out, xnor_2_out, xnor_3_out, xnor_4_out, xnor_5_out, xnor_6_out, xnor_7_out, xnor_8_out, xnor_9_out, xnor_10_out, xnor_11_out, xnor_12_out, xnor_13_out, xnor_14_out, xnor_15_out, xnor_16_out, a[1]);
  and and_36 (and_36_out, not_19_out, xnor_1_out, xnor_2_out, xnor_3_out, xnor_4_out, xnor_5_out, xnor_6_out, xnor_7_out, xnor_8_out, xnor_9_out, xnor_10_out, xnor_11_out, xnor_12_out, xnor_13_out, xnor_14_out, xnor_15_out, xnor_16_out, xnor_17_out, a[0]);
  and a_b_2 (equal, xnor_1_out, xnor_2_out, xnor_3_out, xnor_4_out, xnor_5_out, xnor_6_out, xnor_7_out, xnor_8_out, xnor_9_out, xnor_10_out, xnor_11_out, xnor_12_out, xnor_13_out, xnor_14_out, xnor_15_out, xnor_16_out, xnor_17_out, xnor_18_out);
  nor a_b_3 (a_b_3_out, and_19_out, and_20_out, and_21_out, and_22_out, and_23_out, and_24_out, and_25_out, and_26_out, and_27_out, and_28_out, and_29_out, and_30_out, and_31_out, and_32_out, and_33_out, and_34_out, and_35_out, and_36_out);
  not not_37 (greater, a_b_3_out);
endmodule

// sign comperator
module _18_bit_sign_magnitude_comperator (
  input  [17:0] a,
  input  [17:0] b,
  output greater_a_b_p,
  output equa_a_b_z,
  output less_a_b_n
);

  wire and_4_out, and_5_out, and_6_out, decoder_1_out0, decoder_1_out1, decoder_1_out2, decoder_1_out3,
       n18_bit_unsigned_magnitude_comperator_1_equal, n18_bit_unsigned_magnitude_comperator_1_greater,
       n18_bit_unsigned_magnitude_comperator_1_less, n18_bit_unsigned_magnitude_comperator_2_equal,
       n18_bit_unsigned_magnitude_comperator_2_greater, n18_bit_unsigned_magnitude_comperator_2_less;
  wire [2:0] and_1_out, multiplexer_5_out, multiplexer_6_out, multiplexer_7_out, multiplexer_8_out,
       multiplexer_9_out, or_1_out, or_2_out, or_4_out;
  wire [17:0] multiplexer_1_out, multiplexer_2_out, multiplexer_3_out, multiplexer_4_out;

  Decoder #(.select(2), .enable("false")) decoder_1 (
    .out0(decoder_1_out0), .out1(decoder_1_out1), .out2(decoder_1_out2), .out3(decoder_1_out3),
    .sel({a[17], b[17]}));
  Multiplexer #(.width(18), .disabled(0)) multiplexer_1 (
    .in0(a), .out(multiplexer_1_out), .sel(1'b0), .en(decoder_1_out0));  // open: in1
  Multiplexer #(.width(18), .disabled(0)) multiplexer_2 (
    .in0(b), .out(multiplexer_2_out), .sel(1'b0), .en(decoder_1_out0));  // open: in1
  Multiplexer #(.width(18), .disabled(0)) multiplexer_3 (
    .in0(b), .out(multiplexer_3_out), .sel(1'b0), .en(decoder_1_out3));  // open: in1
  Multiplexer #(.width(18), .disabled(0)) multiplexer_4 (
    .in0(a), .out(multiplexer_4_out), .sel(1'b0), .en(decoder_1_out3));  // open: in1
  _18_bit_unsigned_magnitude_comperator u_18_bit_unsigned_magnitude_comperator_1 (
    .a(multiplexer_1_out), .b(multiplexer_2_out), .greater(n18_bit_unsigned_magnitude_comperator_1_greater),
    .equal(n18_bit_unsigned_magnitude_comperator_1_equal), .less(n18_bit_unsigned_magnitude_comperator_1_less));
  Multiplexer #(.width(3), .disabled(0)) multiplexer_5 (
    .in0(3'b001), .out(multiplexer_5_out), .sel(1'b0), .en(decoder_1_out1));  // open: in1
  Multiplexer #(.width(3), .disabled(0)) multiplexer_6 (
    .in0(3'b100), .out(multiplexer_6_out), .sel(1'b0), .en(decoder_1_out2));  // open: in1
  and and_1 (and_1_out[0], n18_bit_unsigned_magnitude_comperator_1_greater, decoder_1_out0);
  and and_2 (and_1_out[1], n18_bit_unsigned_magnitude_comperator_1_equal, decoder_1_out0);
  and and_3 (and_1_out[2], n18_bit_unsigned_magnitude_comperator_1_less, decoder_1_out0);
  _18_bit_unsigned_magnitude_comperator u_18_bit_unsigned_magnitude_comperator_2 (
    .a(multiplexer_3_out), .b(multiplexer_4_out), .greater(n18_bit_unsigned_magnitude_comperator_2_greater),
    .equal(n18_bit_unsigned_magnitude_comperator_2_equal), .less(n18_bit_unsigned_magnitude_comperator_2_less));
  and and_4 (and_4_out, n18_bit_unsigned_magnitude_comperator_2_greater, decoder_1_out3);
  and and_5 (and_5_out, n18_bit_unsigned_magnitude_comperator_2_less, decoder_1_out3);
  and and_6 (and_6_out, n18_bit_unsigned_magnitude_comperator_2_equal, decoder_1_out3);
  Multiplexer #(.width(3), .disabled(0)) multiplexer_7 (
    .in0(3'b001), .out(multiplexer_7_out), .sel(1'b0), .en(and_4_out));  // open: in1
  Multiplexer #(.width(3), .disabled(0)) multiplexer_8 (
    .in0(3'b010), .out(multiplexer_8_out), .sel(1'b0), .en(and_6_out));  // open: in1
  Multiplexer #(.width(3), .disabled(0)) multiplexer_9 (
    .in0(3'b100), .out(multiplexer_9_out), .sel(1'b0), .en(and_5_out));  // open: in1
  assign or_1_out = and_1_out | multiplexer_5_out;  // OR_Gate or_1, 3 bits wide
  assign or_2_out = multiplexer_7_out | multiplexer_8_out | multiplexer_9_out;  // OR_Gate or_2, 3 bits wide
  assign {less_a_b_n, equa_a_b_z, greater_a_b_p} = or_1_out | or_4_out;  // OR_Gate or_3, 3 bits wide
  assign or_4_out = multiplexer_6_out | or_2_out;  // OR_Gate or_4, 3 bits wide
endmodule
